# Fritzing sketch layout (saved by Fritzing 0.9.9b)
circuit board: 10cm x 25cm
breadboards: 2

parts:
  microSD1 = MicroSD Card Module
  Led_Ring = 24 NeoPixel Ring [part_number=1586]
  Amplifier = Adafruit MAX98357A I2S 3W Class D Amplifier [part_number="Adafruit #3006"]
  Microphone = Adafruit I2S Mic - SPH0645 [part_number="Adafruit #3421"]
  Ambience = Photocell (LDR) [package=THT]
  R3 = Resistor [tolerance=±5% power=0.25 resistance=220 package=THT]
  Volume = POT [package=pot_alpha_rv16af-20]
  R4 = Resistor [tolerance=±5% power=0.25 resistance=4.7k package=THT]
  R7 = Resistor [tolerance=±5% power=0.25 resistance=4.7k package=THT]
  BUTTON3 = Waterproof Pushbutton (red)
  R5 = Resistor [tolerance=±5% power=0.25 resistance=4.7k package=THT]
  R6 = Resistor [tolerance=±5% power=0.25 resistance=4.7k package=THT]
  BUTTON2 = Waterproof Pushbutton (green)
  Off_Switch = SPST Switch [package=r_sw_th]
  BUTTON1 = Waterproof Pushbutton (blue)
  R9 = Resistor [tolerance=±5% resistance=100 power=0.25 package=THT]
  IC1 = MCP23017 I2C I/O Expander
  SPKR1 = Loudspeaker
  R8 = Resistor [tolerance=±5% resistance=100 power=0.25 package=THT]
  R10 = Resistor [tolerance=±5% resistance=100 power=0.25 package=THT]
  SCRN1 = DESPI-C02 ePaper [form="♀ (female rounded)" package=THT]
  BAT1 = Battery Holders [package=battery-aa-panel]  # not connected
  U1 = ESP32S-HiLetgo [part_number=ESP32S-HiLetgo]
  Pad1 = Pad [width=2.8678636557281876 height=1.076508672308546 connect=center]  # not connected
  Pad2 = Pad [width=2.5531012112837437 height=1.1324577904432231 connect=center]  # not connected
  Pad3 = Pad [width=2.4530388140471473 height=1.2325620126654455 connect=center]  # not connected

nets (from the schematic view):
  GND: microSD1.GND, Led_Ring.GND, Amplifier.GND, Amplifier.GAIN, Microphone.GND, Ambience.pin_0, Volume.E, R4.Pin_0, R7.Pin_0, BUTTON3.no_name_yet#5, R5.Pin_0, R6.Pin_0, BUTTON2.no_name_yet#5, Off_Switch.S, BUTTON1.no_name_yet#5, IC1.VSS, IC1.A0, IC1.A1, IC1.A2, SCRN1.GND, U1.GND
  3.3V: microSD1.MISO, Led_Ring.VDD, Amplifier.VIN, Microphone.VDD, R3.Pin_1, Volume.A, BUTTON3.no_name_yet#1, BUTTON2.no_name_yet#1, Off_Switch.O, BUTTON1.no_name_yet#1, IC1.VDD, IC1.RESET, SCRN1.PWR, U1.3.3
  N1: microSD1.CLK, U1.GPIO19
  N2: microSD1.MOSI, U1.GPIO23
  N3: microSD1.CS, U1.GPIO18
  N4: microSD1.3V3, U1.GPIO5
  N5: Led_Ring.IN, U1.GPIO0
  N6: Amplifier.DIN, U1.GPIO32
  N7: Amplifier.BCLK, U1.GPIO25
  N8: Amplifier.LRCLK, U1.GPIO33
  N9: Amplifier.VO-, SPKR1.pin1
  N10: Amplifier.VO+, SPKR1.pin2
  N11: Microphone.BCLK, U1.GPIO17
  N12: Microphone.DATA, U1.GPIO16
  N13: Microphone.WS, U1.GPIO4
  N14: Ambience.pin_1, R3.Pin_0, U1.GPIO39
  N15: Volume.S, U1.GPIO36
  N16: R4.Pin_1, Off_Switch.P, IC1.GPA7
  N17: R7.Pin_1, BUTTON3.no_name_yet#2, IC1.GPA2
  N18: BUTTON3.no_name_yet#4, R10.Pin_1
  N19: R5.Pin_1, BUTTON1.no_name_yet#2, IC1.GPA6
  N20: R6.Pin_1, BUTTON2.no_name_yet#2, IC1.GPA4
  N21: BUTTON2.no_name_yet#4, R9.Pin_1
  N22: BUTTON1.no_name_yet#4, R8.Pin_1
  N23: R9.Pin_0, IC1.GPA3
  N24: IC1.SCL, U1.GPIO22
  N25: IC1.SDA, U1.GPIO21
  N26: IC1.INTA, U1.GPIO35
  N27: IC1.GPA1, R10.Pin_0
  N28: IC1.GPA5, R8.Pin_0
  N29: SCRN1.BUSY, U1.GPIO26
  N30: SCRN1.RES, U1.GPIO13
  N31: SCRN1.D/C, U1.GPIO12
  N32: SCRN1.CS, U1.GPIO15
  N33: SCRN1.SCK, U1.GPIO14
  N34: SCRN1.SDI, U1.GPIO27

custom parts:
  MicroSD Card Module: A common microSD card module.
  24 NeoPixel Ring: 24 ultra bright smart LED NeoPixels are arranged in a circle with 2.6" (66mm) outer diameter. The rings are 'chainable' - connect the output pin of one to the input pin of another. Use only one microcontroller pin to control as many as you can chain together! Each LED is addressable as the driver chip is inside the LED. Each one has ~18mA constant current drive so the color will be very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
  Adafruit MAX98357A I2S 3W Class D Amplifier: Listen to this good news - we now have an all in one digital audio amp breakout board that works incredibly well with the Raspberry Pi! If you're looking for an easy and low cost way to get you digital sound files bumpin' then the MAX08357 I2S Amp Breakout is for you. It takes standard I2S digital audio input and, not only decodes it into analog, but also amplifies it directly into a speaker.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
  Adafruit I2S Mic - SPH0645: For many microcontrollers, adding audio input is easy with one of our analog microphone breakouts. But as you get to bigger and better microcontrollers and microcomputers, you'll find that you don't always have an analog input, or maybe you want to avoid the noise that can seep in with an analog mic system. Once you get past 8-bit micros, you will often find an I2S peripheral, that can take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
  Waterproof Pushbutton (red): Waterproof Illuminated Pushbutton (red)
  Waterproof Pushbutton (green): Waterproof Illuminated Pushbutton (green)
  Waterproof Pushbutton (blue): Waterproof Illuminated Pushbutton (blue)
  MCP23017 I2C I/O Expander: The MCP23017 uses two i2c pins (these can be shared with other i2c devices), and in exchange gives you 16 general purpose pins. You can set each of 16 pins to be input, output, input with a pullup or open drain. There's even the ability to get an interrupt via an external pin when any of the inputs change so you don't have to keep polling the chip.
  ESP32S-HiLetgo: HiLetgo ESP-WROOM-32 ESP32 ESP-32S Development Board 2.4GHz Dual-Mode WiFi + Bluetooth Dual Cores Microcontroller The ESP32 integrated with Antenna switches, RF Balun, power amplifiers, low-noise amplifiers, filters, and management modules, and the entire solution occupies the least area of PCB. 2.4 GHz Wi-Fi plus Bluetooth dual-mode chip, with TSMC Ultra-low power consumption 40nm technology,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
